// Logisim project RTL.circ as structural Verilog: 1 circuit, main circuit main
module main (
  input  mk,
  input  wk,
  input  mcont,
  input  wrsize,
  input  wrcont,
  input  rst0,
  input  wrtempo,
  input  ms,
  input  ennd,
  input  [1:0] entrada,
  input  rstb,
  input  wrbot,
  input  azulB,
  input  verdeB,
  input  amreloB,
  input  vermelhoB,
  input  mlf,
  input  wrlf,
  input  rst,
  output [7:0] add,
  output igualt,
  output azulLuz,
  output vermelhoLuz,
  output amareloLuz,
  output verdeLuz,
  output fim2,
  output fim,
  output sai,
  output [1:0] ft,
  output fica
);

  wire and_2_out, and_3_out, and_4_out, and_5_out, and_6_out, and_7_out, and_8_out, and_9_out,
       comparator_2_eq, or_1_out;
  wire [1:0] ff1_q, ff2_q, multiplexer_4_out, xor_1_out;
  wire [2:0] adder_4_out, cnt_q, multiplexer_3_out;
  wire [3:0] botao_q, decoder_1_out0, multiplexer_2_out, mx_q;
  wire [7:0] adder_1_out, adder_2_out, adder_3_out, multiplexer_1_out, resize_q;

  Adder adder_1 (.a(add), .b(8'h1), .out(adder_1_out));  // open: cin, cout
  Multiplexer #(.width(8), .enable("false")) multiplexer_1 (
    .in0({8{1'b0}}), .in1(adder_1_out), .out(multiplexer_1_out), .sel(mk));
  Adder adder_2 (.a(resize_q), .b(8'h1), .out(adder_2_out));  // open: cin, cout
  Register k (.D(multiplexer_1_out), .en(wk), .Q(add), .clr(rst0));  // open: clk
  Register resize (.D(adder_2_out), .en(wrsize), .Q(resize_q), .clr(rst0));  // open: clk
  Decoder #(.select(2), .enable("false")) decoder_1 (
    .out0(decoder_1_out0[0]), .out1(decoder_1_out0[1]), .out2(decoder_1_out0[2]), .out3(decoder_1_out0[3]),
    .sel(entrada));
  Adder adder_3 (.a(add), .b(8'h1), .out(adder_3_out));  // open: cin, cout
  Comparator comparator_1 (.a(add), .b(resize_q), .eq(fim));  // open: gt, lt
  Comparator #(.width(4)) comparator_2 (.a(decoder_1_out0), .b(botao_q), .eq(comparator_2_eq));  // open: gt, lt
  Comparator comparator_3 (.a(adder_3_out), .b(resize_q), .eq(fim2));  // open: gt, lt
  not not_1 (sai, comparator_2_eq);
  Multiplexer #(.width(4), .enable("false")) multiplexer_2 (
    .in0(decoder_1_out0), .in1(botao_q), .out(multiplexer_2_out), .sel(ms));
  Register #(.width(4)) botao (
    .D({amreloB, verdeB, vermelhoB, azulB}), .en(wrbot), .Q(botao_q), .clr(or_1_out));  // open: clk
  Adder #(.width(3)) adder_4 (.a(3'b001), .b(cnt_q), .out(adder_4_out));  // open: cin, cout
  Register #(.width(4)) mx (.D(multiplexer_2_out), .en(wrtempo), .Q(mx_q), .clr(rst0));  // open: clk
  or or_1 (or_1_out, rst0, rstb, wrlf);
  and and_1 (fica, ~azulB, ~vermelhoB, ~verdeB, ~amreloB);  // AND_Gate
  Multiplexer #(.width(3), .enable("false")) multiplexer_3 (
    .in0(3'b000), .in1(adder_4_out), .out(multiplexer_3_out), .sel(mcont));
  Register #(.width(3)) cnt (.D(multiplexer_3_out), .en(wrcont), .Q(cnt_q), .clr(rst0));  // open: clk
  and and_2 (and_2_out, ~mx_q[0], mx_q[1], mx_q[2], mx_q[3]);  // AND_Gate
  and and_3 (and_3_out, mx_q[0], ~mx_q[1], mx_q[2], mx_q[3]);  // AND_Gate
  and and_4 (and_4_out, mx_q[0], mx_q[1], ~mx_q[2], mx_q[3]);  // AND_Gate
  and and_5 (and_5_out, mx_q[0], mx_q[1], mx_q[2], ~mx_q[2]);  // AND_Gate
  Comparator #(.width(3)) comparator_4 (.a(cnt_q), .b(3'b010), .eq(igualt));  // open: gt, lt
  and and_6 (and_6_out, and_2_out, ennd);
  and and_7 (and_7_out, and_3_out, ennd);
  and and_8 (and_8_out, and_4_out, ennd);
  and and_9 (and_9_out, and_5_out, ennd);
  assign xor_1_out = ft ^ ff1_q;  // XOR_Gate xor_1, 2 bits wide
  assign azulLuz = and_6_out ? 1'b1 : 1'bz;  // Controlled_Buffer controlled_buffer_1
  assign vermelhoLuz = and_7_out ? 1'b1 : 1'bz;  // Controlled_Buffer controlled_buffer_2
  assign amareloLuz = and_8_out ? 1'b1 : 1'bz;  // Controlled_Buffer controlled_buffer_3
  assign verdeLuz = and_9_out ? 1'b1 : 1'bz;  // Controlled_Buffer controlled_buffer_4
  Multiplexer #(.width(2), .enable("false")) multiplexer_4 (
    .in0(2'b01), .in1(ff1_q), .out(multiplexer_4_out), .sel(mlf));
  Register #(.width(2)) ff0 (.D(multiplexer_4_out), .en(wrlf), .Q(ft), .clr(rst));  // open: clk
  Register #(.width(2)) ff1 (.D(ff2_q), .en(wrlf), .Q(ff1_q), .clr(rst));  // open: clk
  Register #(.width(2)) ff2 (.D(xor_1_out), .en(wrlf), .Q(ff2_q), .clr(rst));  // open: clk
endmodule
